# Fritzing sketch Four_LEDs (saved by Fritzing 0.9.3b)
breadboards: 1

parts:
  Часть1 = Arduino Mega 2560 (Rev3)
  LED1 = LED - 5mm [color="Red (633nm)" package="5 mm [THT]"]
  LED2 = LED - 5mm [color="Red (633nm)" package="5 mm [THT]"]
  LED3 = LED - 5mm [color="Red (633nm)" package="5 mm [THT]"]
  LED4 = LED - 5mm [color="Red (633nm)" package="5 mm [THT]"]
  R1 = Resistor [tolerance=±5% resistance=220 package=THT]

nets:
  N1: Часть1.D18/TX1, LED4.cathode
  N2: Часть1.D17_PWM/RX2, LED3.cathode
  N3: Часть1.D16_PWM/TX2, LED2.cathode
  N4: Часть1.D15/RX3, LED1.cathode
  N5: Часть1.GND, R1.Pin_1
  N6: LED1.anode, LED2.anode, LED3.anode, LED4.anode, R1.Pin_0
