# Fritzing sketch Four_LEDs_and_button (saved by Fritzing 0.9.3b)
breadboards: 1

parts:
  Часть1 = Arduino Mega 2560 (Rev3)
  S1 = Pushbutton [package="[THT]"]
  LED1 = LED - 5mm [color="Red (633nm)" package="5 mm [THT]"]
  LED2 = LED - 5mm [color="Red (633nm)" package="5 mm [THT]"]
  LED3 = LED - 5mm [color="Red (633nm)" package="5 mm [THT]"]
  LED4 = LED - 5mm [color="Red (633nm)" package="5 mm [THT]"]
  R1 = Resistor [tolerance=±5% resistance=220 package=THT]
  R2 = Resistor [tolerance=±5% resistance=220 package=THT]

nets:
  N1: Часть1.D18/TX1, LED4.cathode
  N2: Часть1.D17_PWM/RX2, LED3.cathode
  N3: Часть1.D16_PWM/TX2, LED2.cathode
  N4: Часть1.D15/RX3, LED1.cathode
  N5: Часть1.GND, Часть1.D2_PWM, S1.Pin_1, S1.Pin_2, R1.Pin_1, R2.Pin_0
  N6: S1.Pin_3, S1.Pin_4, R2.Pin_1
  N7: LED1.anode, LED2.anode, LED3.anode, LED4.anode, R1.Pin_0
