# Fritzing sketch IR_sensor_HC-SR501 (saved by Fritzing 0.9.3b)

parts:
  Arduino_UNO = Arduino Uno (Rev3)
  Sensore_PIR_HC-SR501 = HC-SR501 Body Sensor Module
  LED1 = LED - 5mm [color="Red (633nm)" package="5 mm [THT]"]

nets:
  N1: Arduino_UNO.D13/SCK, LED1.anode
  GND: Arduino_UNO.GND, Sensore_PIR_HC-SR501.GND, LED1.cathode
  N2: Arduino_UNO.D2, Sensore_PIR_HC-SR501.OUT
  5V: Arduino_UNO.5V, Sensore_PIR_HC-SR501.VCC

custom parts:
  HC-SR501 Body Sensor Module: Pyroelectric Infrared PIR Motion Sensor Detector Module
