# Fritzing sketch Joystick_improved (saved by Fritzing 0.8.5b)
breadboards: 1

parts:
  Часть1 = Arduino Mega 2560 (Rev3)
  LED3 = LED - 5mm [color="Red (633nm)" package="5 mm [THT]"]
  LED4 = LED - 5mm [color="Red (633nm)" package="5 mm [THT]"]
  LED5 = LED - 5mm [color="Red (633nm)" package="5 mm [THT]"]
  LED7 = LED - 5mm [color="Red (633nm)" package="5 mm [THT]"]
  Часть2 = Thumb Joystick
  LED8 = LED - 5mm [color="Red (633nm)" package="5 mm [THT]"]

nets:
  N1: Часть1.A1, Часть2.VERT
  N2: Часть1.A3, Часть2.HORZ
  N3: Часть1.D11_PWM, Часть2.SEL
  N4: Часть1.D9_PWM, LED3.cathode
  N5: Часть1.D8_PWM, LED4.cathode
  5V: Часть1.5V, Часть2.VCC
  GND: Часть1.GND, LED3.anode, LED4.anode, LED5.anode, LED7.anode, Часть2.GND, LED8.anode
  N6: Часть1.D3_PWM, LED7.cathode
  N7: Часть1.D5_PWM, LED8.cathode
  N8: Часть1.D6_PWM, LED5.cathode
