# Fritzing sketch Joystick_simple (saved by Fritzing 0.8.5b)

parts:
  Часть1 = Arduino Mega 2560 (Rev3)
  Часть2 = Thumb Joystick

nets:
  N1: Часть1.A1, Часть2.VERT
  N2: Часть1.A3, Часть2.HORZ
  N3: Часть1.D11_PWM, Часть2.SEL
  5V: Часть1.5V, Часть2.VCC
  GND: Часть1.GND, Часть2.GND
